// Logisim project s-mips.circ as structural Verilog: 13 circuits, main circuit S-MIPS Board
module S_MIPS_Board (
  input  DESHABILITAR_DISPATCHER,
  output halt
);

  wire button_1_out, CLK, CS, d_ff_1_q, LCLR, LoadRAM, LoadRAMOn, LW, R_R_W, R_W, ram_dispatcher_1_finished,
       RCS, Reset_out, RST, TTY_EN;
  wire [2:0] KDB;
  wire [3:0] LMask, Mask, ram_1_read_time, ram_1_write_time, RMask;
  wire [6:0] KDB_DATA, TTY_DATA;
  wire [15:0] Addr, LAddr, RAddr;
  wire [31:0] I0, I1, I2, I3, LData, ram_1_data_out_0, ram_1_data_out_1, ram_1_data_out_2, ram_1_data_out_3,
       RI0, RI1, RI2, RI3;

  TTY #(.rows(25), .cols(80)) tty_1 (.data(TTY_DATA), .clk(CLK), .we(TTY_EN), .clr(RST));
  not not_1 (LoadRAMOn, ram_dispatcher_1_finished);
  RAM_Dispatcher ram_dispatcher_1 (
    .WriteTime(ram_1_write_time), .Clock(CLK), .Data(LData), .Address(LAddr), .Mask(LMask),
    .Finished(ram_dispatcher_1_finished), .Write(LW), .CLR(LCLR));
  Keyboard #(.buflen(64)) keyboard_1 (.clk(CLK), .re(KDB[0]), .avail(KDB[2]), .data(KDB_DATA));  // open: clr
  RAM ram_1 (
    .Address(RAddr), .Data_Out_0(ram_1_data_out_0), .Data_Out_1(ram_1_data_out_1),
    .Data_Out_2(ram_1_data_out_2), .Data_Out_3(ram_1_data_out_3), .Data_In_0(RI0), .Data_In_1(RI1),
    .Data_In_2(RI2), .Data_In_3(RI3), .Mask(RMask), .nRead_Write(R_R_W), .Chip_Select(RCS),
    .Read_Time(ram_1_read_time), .Reset(button_1_out), .Write_Time(ram_1_write_time));
  Button button_1 (.out(button_1_out));
  D_Flip_Flop d_ff_1 (.clk(CLK), .D(1'b1), .Q(d_ff_1_q), .reset(Reset_out));  // open: Qn, preset, en
  Button Reset (.out(Reset_out));
  S_MIPS s_mips_1 (
    .Kbd_Enable(KDB[0]), .Address(Addr), .Kbd_Clear(KDB[1]), .Kbd_Available(KDB[2]), .RAM_In_0(I0),
    .Kbd_ASCII_Data(KDB_DATA), .RAM_In_1(I1), .TTY_Enable(TTY_EN), .RAM_In_2(I2), .RAM_In_3(I3),
    .TTY_ASCII_Data(TTY_DATA), .Reset(RST), .RAM_Out_0(ram_1_data_out_0), .Clock(CLK),
    .RAM_Out_1(ram_1_data_out_1), .Stop(halt), .RAM_Out_2(ram_1_data_out_2), .RAM_Out_3(ram_1_data_out_3),
    .Mask(Mask), .Read_Time(ram_1_read_time), .Write_Time(ram_1_write_time), .nRead_Write(R_W),
    .Chip_Select(CS));
  D_Flip_Flop d_ff_2 (.clk(CLK), .D(d_ff_1_q), .Qn(LCLR), .reset(Reset_out));  // open: Q, preset, en
  or or_1 (RST, LCLR, LoadRAM);
  Clock clock_1 (.out(CLK));
  Multiplexer #(.width(32), .enable("false")) multiplexer_1 (.in0(I0), .in1(LData), .out(RI0), .sel(LoadRAM));
  Multiplexer #(.width(32), .enable("false")) multiplexer_2 (.in0(I1), .in1(LData), .out(RI1), .sel(LoadRAM));
  Multiplexer #(.width(32), .enable("false")) multiplexer_3 (.in0(I2), .in1(LData), .out(RI2), .sel(LoadRAM));
  Multiplexer #(.width(32), .enable("false")) multiplexer_4 (.in0(I3), .in1(LData), .out(RI3), .sel(LoadRAM));
  and and_1 (LoadRAM, ~DESHABILITAR_DISPATCHER, LoadRAMOn);  // AND_Gate
  Multiplexer #(.width(16), .enable("false")) multiplexer_5 (.in0(Addr), .in1(LAddr), .out(RAddr), .sel(LoadRAM));
  Multiplexer #(.width(4), .enable("false")) multiplexer_6 (.in0(Mask), .in1(LMask), .out(RMask), .sel(LoadRAM));
  Multiplexer #(.enable("false")) multiplexer_7 (.in0(CS), .in1(LW), .out(RCS), .sel(LoadRAM));
  Multiplexer #(.enable("false")) multiplexer_8 (.in0(R_W), .in1(LW), .out(R_R_W), .sel(LoadRAM));

  // Notes on the sheet:
  //   NO MODIFICAR
  //   Keyboard
endmodule

module RAM (
  input  [15:0] Address,
  input  [31:0] Data_In_0,
  input  [31:0] Data_In_1,
  input  [31:0] Data_In_2,
  input  [31:0] Data_In_3,
  input  [3:0] Mask,
  input  nRead_Write,
  input  Chip_Select,
  input  Reset,
  output [31:0] Data_Out_0,
  output [31:0] Data_Out_1,
  output [31:0] Data_Out_2,
  output [31:0] Data_Out_3,
  output [3:0] Read_Time,
  output [3:0] Write_Time
);

  wire and_2_out, and_3_out, and_4_out, and_5_out, and_6_out, and_7_out, and_8_out, and_9_out, Changed, CLK,
       comparator_2_eq, comparator_3_eq, comparator_4_eq, comparator_5_eq, comparator_6_eq, Count,
       demultiplexer_3_out0, Idle, Idle_q, Load, Load0, Load1, nand_1_out, or_1_out, or_2_out, or_3_out,
       or_4_out, or_5_out, or_6_out, or_7_out, or_8_out, or_9_out, or_10_out, Proc_q, Update_Mem, Zero_Time;
  wire [3:0] counter_1_q, multiplexer_1_out, subtractor_1_out;
  wire [31:0] register_1_q, register_2_q, register_3_q, register_4_q, register_5_q;

  // Probe on 4'b0011
  // Probe on 4'b0010
  Multiplexer #(.width(4), .enable("false")) multiplexer_1 (
    .in0(4'b0011), .in1(4'b0010), .out(multiplexer_1_out), .sel(nRead_Write));
  or or_1 (or_1_out, Idle, Update_Mem);
  or or_2 (or_2_out, ~Chip_Select, Reset);  // OR_Gate
  Subtractor #(.width(4)) subtractor_1 (.a(multiplexer_1_out), .b(4'b0010), .out(subtractor_1_out));  // open: bin, bout
  D_Flip_Flop u_Idle (.clk(CLK), .D(or_1_out), .Q(Idle_q), .preset(or_2_out));  // open: Qn, en, reset
  Demultiplexer #(.enable("false")) demultiplexer_1 (.out0(Idle), .out1(Load0), .in(Idle_q), .sel(Changed));
  // Probe on counter_1_q
  Counter #(.width(4), .max('hf)) counter_1 (
    .load(Load), .D(subtractor_1_out), .count(Count), .Q(counter_1_q), .clk(CLK), .clr(or_3_out));  // open: carry
  or or_3 (or_3_out, ~Chip_Select, Reset);  // OR_Gate
  Comparator #(.width(4), .mode("unsigned")) comparator_1 (
    .a(4'b0000), .b(counter_1_q), .eq(Zero_Time));  // open: gt, lt
  or or_4 (or_4_out, Count, Load0, Load1);
  Register #(.width(32)) register_1 (.D(Data_In_0), .en(Chip_Select), .Q(register_1_q), .clk(CLK), .clr(or_5_out));
  or or_5 (or_5_out, ~Chip_Select, Reset);  // OR_Gate
  Register #(.width(32)) register_2 (.D(Data_In_1), .en(Chip_Select), .Q(register_2_q), .clk(CLK), .clr(or_6_out));
  or or_6 (or_6_out, ~Chip_Select, Reset);  // OR_Gate
  Register #(.width(32)) register_3 (.D(Data_In_2), .en(Chip_Select), .Q(register_3_q), .clk(CLK), .clr(or_7_out));
  or or_7 (or_7_out, ~Chip_Select, Reset);  // OR_Gate
  Register #(.width(32)) register_4 (.D(Data_In_3), .en(Chip_Select), .Q(register_4_q), .clk(CLK), .clr(or_8_out));
  or or_8 (or_8_out, ~Chip_Select, Reset);  // OR_Gate
  Register #(.width(32)) register_5 (
    .D({{11{1'b1}}, nRead_Write, Mask, Address}), .en(Chip_Select), .Q(register_5_q), .clk(CLK),
    .clr(or_9_out));
  or or_9 (or_9_out, ~Chip_Select, Reset);  // OR_Gate
  D_Flip_Flop Proc (.clk(CLK), .D(or_4_out), .Q(Proc_q), .reset(or_10_out));  // open: Qn, preset, en
  or or_10 (or_10_out, ~Chip_Select, Reset);  // OR_Gate
  Demultiplexer #(.enable("false")) demultiplexer_2 (
    .out0(Count), .out1(Update_Mem), .in(demultiplexer_3_out0), .sel(Zero_Time));
  Demultiplexer #(.enable("false")) demultiplexer_3 (
    .out0(demultiplexer_3_out0), .out1(Load1), .in(Proc_q), .sel(Changed));
  Clock clock_1 (.out(CLK));
  Comparator #(.width(32)) comparator_2 (.a(register_1_q), .b(Data_In_0), .eq(comparator_2_eq));  // open: gt, lt
  Comparator #(.width(32)) comparator_3 (.a(register_2_q), .b(Data_In_1), .eq(comparator_3_eq));  // open: gt, lt
  Comparator #(.width(32)) comparator_4 (.a(register_3_q), .b(Data_In_2), .eq(comparator_4_eq));  // open: gt, lt
  Comparator #(.width(32)) comparator_5 (.a(register_4_q), .b(Data_In_3), .eq(comparator_5_eq));  // open: gt, lt
  Comparator #(.width(32)) comparator_6 (
    .a(register_5_q), .b({{11{1'b1}}, nRead_Write, Mask, Address}), .eq(comparator_6_eq));  // open: gt, lt
  nand nand_1 (nand_1_out, comparator_6_eq, comparator_2_eq, comparator_3_eq, comparator_4_eq, comparator_5_eq);
  and and_1 (Changed, nand_1_out, Chip_Select);
  or or_11 (Load, Count, Load1, Load0);
  and and_2 (and_2_out, Mask[0], Update_Mem, nRead_Write);
  and and_3 (and_3_out, Mask[1], Update_Mem, nRead_Write);
  and and_4 (and_4_out, Mask[2], Update_Mem, nRead_Write);
  and and_5 (and_5_out, Mask[3], Update_Mem, nRead_Write);
  RAM_part #(.addrWidth(16), .dataWidth(32), .bus("separate")) ram_1 (
    .addr(Address), .din(Data_In_0), .data(Data_Out_0), .str(and_2_out), .sel(Chip_Select), .clk(CLK),
    .ld(and_6_out), .clr(Reset));
  and and_6 (and_6_out, ~nRead_Write, Idle);  // AND_Gate
  RAM_part #(.addrWidth(16), .dataWidth(32), .bus("separate")) ram_2 (
    .addr(Address), .din(Data_In_1), .data(Data_Out_1), .str(and_3_out), .sel(Chip_Select), .clk(CLK),
    .ld(and_7_out), .clr(Reset));
  and and_7 (and_7_out, ~nRead_Write, Idle);  // AND_Gate
  RAM_part #(.addrWidth(16), .dataWidth(32), .bus("separate")) ram_3 (
    .addr(Address), .din(Data_In_2), .data(Data_Out_2), .str(and_4_out), .sel(Chip_Select), .clk(CLK),
    .ld(and_8_out), .clr(Reset));
  and and_8 (and_8_out, ~nRead_Write, Idle);  // AND_Gate
  RAM_part #(.addrWidth(16), .dataWidth(32), .bus("separate")) ram_4 (
    .addr(Address), .din(Data_In_3), .data(Data_Out_3), .str(and_5_out), .sel(Chip_Select), .clk(CLK),
    .ld(and_9_out), .clr(Reset));
  and and_9 (and_9_out, ~nRead_Write, Idle);  // AND_Gate

  assign Read_Time = 4'b0011;
  assign Write_Time = 4'b0010;

  // Other names for the same wires on the sheet: M0 = Mask[0]; M1 = Mask[1]; M2 = Mask[2]; M3 = Mask[3];
  //   RW = nRead_Write; CLR = Reset; CS = Chip_Select; Load2 = Count

  // Notes on the sheet:
  //   NO MODIFICAR
  //   excepto quizás los valores RT y WT
  //   BANK0
  //   BANK1
  //   BANK2
  //   BANK3
endmodule

module S_MIPS (
  input  Kbd_Available,
  input  [6:0] Kbd_ASCII_Data,
  input  [31:0] RAM_Out_0,
  input  [31:0] RAM_Out_1,
  input  Reset,
  input  [31:0] RAM_Out_2,
  input  Clock,
  input  [31:0] RAM_Out_3,
  input  [3:0] Read_Time,
  input  [3:0] Write_Time,
  output Kbd_Enable,
  output [15:0] Address,
  output Kbd_Clear,
  output TTY_Enable,
  output [6:0] TTY_ASCII_Data,
  output Stop,
  output [31:0] RAM_In_0,
  output [31:0] RAM_In_1,
  output [31:0] RAM_In_2,
  output [31:0] RAM_In_3,
  output [3:0] Mask,
  output nRead_Write,
  output Chip_Select
);


  // Other names for the same wires on the sheet: CLK = Clock; CLR = Reset; CS = Chip_Select;
  //   KBD_AVAIL = Kbd_Available; KBD_CLR = Kbd_Clear; KBD_DATA[6:0] = Kbd_ASCII_Data; RAM_A[15:0] = Address;
  //   RAM_INPUT_0[31:0] = RAM_In_0; RAM_INPUT_1[31:0] = RAM_In_1; RAM_INPUT_2[31:0] = RAM_In_2;
  //   RAM_INPUT_3[31:0] = RAM_In_3; RAM_MASK[3:0] = Mask; RAM_OUTPUT_0[31:0] = RAM_Out_0;
  //   RAM_OUTPUT_1[31:0] = RAM_Out_1; RAM_OUTPUT_2[31:0] = RAM_Out_2; RAM_OUTPUT_3[31:0] = RAM_Out_3;
  //   RW = nRead_Write; TTY_DATA[6:0] = TTY_ASCII_Data

  // Notes on the sheet:
  //   RAM ADDRESS
  //   DATA FROM RAM
  //   DATA TO RAM
  //   DATA WRITE MASK
  //   RAM TIMING
  //   RAM CONTROL
  //   KEYBOARD
  //   TTY
  //   SEQUENCING
endmodule

module RAM_Dispatcher (
  input  [3:0] WriteTime,
  input  Clock,
  input  CLR,
  output [31:0] Data,
  output [15:0] Address,
  output [3:0] Mask,
  output Finished,
  output Write
);

  wire demultiplexer_2_out1, demultiplexer_3_out1, End, IDLE_q, IncAddr, Load, or_1_out, or_2_out, While_q,
       WriteEnd;
  wire [3:0] counter_1_q;
  wire [31:0] CurrentAddress_q;

  Counter #(.width(32), .max('hffffffff)) CurrentAddress (
    .count(IncAddr), .Q({CurrentAddress_q[31:18], Address, CurrentAddress_q[1:0]}), .clk(Clock), .clr(CLR));  // open: load, D, carry
  or or_1 (or_1_out, IncAddr, demultiplexer_3_out1, Finished);
  D_Flip_Flop IDLE (.clk(Clock), .D(or_1_out), .Q(IDLE_q), .preset(CLR));  // open: Qn, en, reset
  Demultiplexer #(.enable("false")) demultiplexer_1 (.out0(Load), .out1(Finished), .in(IDLE_q), .sel(End));
  D_Flip_Flop While (.clk(Clock), .D(or_2_out), .Q(While_q), .reset(CLR));  // open: Qn, preset, en
  or or_2 (or_2_out, Write, Load);
  RAM_part #(.addrWidth(18), .dataWidth(32)) ram_1 (
    .addr({Address, CurrentAddress_q[1:0]}), .data(Data), .clk(Clock));  // open: sel, ld, clr
  Demultiplexer #(.enable("false")) demultiplexer_2 (
    .out0(Write), .out1(demultiplexer_2_out1), .in(While_q), .sel(WriteEnd));
  Decoder #(.select(2)) decoder_1 (
    .out0(Mask[0]), .out1(Mask[1]), .out2(Mask[2]), .out3(Mask[3]), .sel(CurrentAddress_q[1:0]));  // open: en
  Demultiplexer #(.enable("false")) demultiplexer_3 (
    .out0(IncAddr), .out1(demultiplexer_3_out1), .in(demultiplexer_2_out1), .sel(End));
  Counter #(.width(4), .max('hf)) counter_1 (
    .load(Load), .D(WriteTime), .count(Write), .Q(counter_1_q), .clk(Clock));  // open: carry, clr
  Comparator #(.width(32)) comparator_1 (.a(Data), .b({32{1'b1}}), .eq(End));  // open: gt, lt
  Comparator #(.width(4)) comparator_2 (.a(4'b0000), .b(counter_1_q), .eq(WriteEnd));  // open: gt, lt

  // Other names for the same wires on the sheet: CLK = Clock; Count = Write; WT[3:0] = WriteTime
endmodule

module Data_Path (
  input  in_1,
  input  [1:0] in_2,
  input  [2:0] in_3,
  input  in_4,
  input  [1:0] in_5,
  input  [3:0] in_6,
  input  in_7,
  input  [1:0] in_8,
  input  in_9,
  input  [2:0] in_10,
  input  in_11,
  input  in_12,
  input  in_13,
  input  [31:0] in_14,
  input  in_15,
  input  [6:0] in_16,
  input  in_17,
  input  in_18,
  input  in_19,
  input  in_20,
  input  in_21,
  output [5:0] out_22,
  output out_23,
  output [31:0] out_24,
  output [31:0] out_25,
  output [5:0] out_26,
  output out_27,
  output [6:0] out_28
);

  wire [4:0] Rd, Rs, Rt, SDA;
  wire [5:0] Op_Code;
  wire [15:0] Const;
  wire [25:0] Jump_Rute, Rute;
  wire [31:0] ALU, bit_extender_1_out, DA, DATA, Hi, High, Inst, KDP, Lo, Low, Offset, PC, PC_prime,
       Rand_Generator, Rd_prime, RS__prime, RT__prime, RT_t, Sp;
  wire [31:7] RS_t;

  Program_Counter program_counter_1 (.in_1(PC_prime), .in_2(in_21), .in_3(in_13), .in_4(in_18), .out_5(PC));
  Branch_Control branch_control_1 (
    .in_1(PC), .in_2(Rute), .in_3(Offset), .in_4(in_10), .in_5({RS_t, out_28}), .out_8(PC_prime),
    .in_6(out_23), .in_7(out_27));
  assign bit_extender_1_out = {{25{1'b0}}, in_16};  // Bit_Extender bit_extender_1
  Random #(.width(32)) random_1 (.clk(in_21), .next(in_21), .out(Rand_Generator));  // open: clr
  Multiplexer #(.width(32)) multiplexer_1 (
    .in0({32{1'b1}}), .in1(bit_extender_1_out), .out(KDP), .sel(in_17));  // open: en
  Intruction_Decoder intruction_decoder_1 (
    .out_2(Op_Code), .out_3(Rs), .out_4(Rt), .out_5(Jump_Rute), .out_6(Rd), .out_7(Const), .out_8(out_26),
    .in_1(Inst));
  Register #(.width(32)) register_1 (.D(in_14), .en(in_15), .Q(Inst), .clk(in_21), .clr(in_18));
  Register #(.width(32)) register_2 (.D(in_14), .en(in_21), .Q(DATA), .clk(in_21), .clr(in_18));
  Register_File register_file_1 (
    .in_1(DA), .in_2(Rs), .in_3(Rt), .in_4(SDA), .in_5(in_21), .in_7(in_1), .in_9(in_18),
    .out_10({RS_t, out_28}), .out_11(RT_t), .out_12(Sp), .in_6(in_20), .in_8(in_19));
  Multiplexer #(.select(2), .width(5)) multiplexer_2 (
    .in0(Rs), .in1(Rt), .in2({5{1'b1}}), .out(SDA), .sel(in_2));  // open: in3, en
  Multiplexer #(.select(3), .width(32)) multiplexer_3 (
    .in0(ALU), .in1(DATA), .in2(High), .in3(Low), .in4(Rand_Generator), .in5(KDP), .out(DA), .sel(in_3));  // open: in6, in7, en
  Sign_Extender sign_extender_1 (.in_1(Const), .in_2(in_4), .out_3(Offset));
  Multiplexer #(.select(2), .width(32)) multiplexer_4 (
    .in0(RT_t), .in1(32'h4), .in2(Offset), .out(RT__prime), .sel(in_8));  // open: in3, en
  Multiplexer #(.width(32)) multiplexer_5 (.in0({RS_t, out_28}), .in1(Sp), .out(RS__prime), .sel(in_7));  // open: en
  ALU alu_1 (
    .in_1(RS__prime), .in_2(RT__prime), .in_3(in_6), .out_4(Rd_prime), .out_5(Hi), .out_6(Lo),
    .out_7(out_23), .out_8(out_27));
  Register #(.width(32)) register_3 (.D(Hi), .en(in_6[3]), .Q(High), .clk(in_21), .clr(in_18));
  Register #(.width(32)) register_4 (.D(Lo), .en(in_6[3]), .Q(Low), .clk(in_21), .clr(in_18));
  Register #(.width(32)) register_5 (.D(Rd_prime), .en(in_11), .Q(ALU), .clk(in_21), .clr(in_18));
  Multiplexer #(.width(32)) multiplexer_6 (.in0({RS_t, out_28}), .in1(RT_t), .out(out_25), .sel(in_9));  // open: en
  Multiplexer #(.select(2), .width(32)) multiplexer_7 (
    .in0(PC), .in1(ALU), .in2(Sp), .out(out_24), .sel(in_5));  // open: in3, en

  assign in_12 = in_6[3];

  // Other names for the same wires on the sheet: Adress[31:0] = out_24; Adress_Select[1:0] = in_5;
  //   ALU_Select[3:0] = in_6; Hi_Lo_Enable = in_6[3]; ALU_Select_A = in_7; ALU_Select_B[1:0] = in_8; BS[2:0] = in_10;
  //   clk = in_21; DA_Select[1:0] = in_2; Data_Select[2:0] = in_3; Enable_ALU_Result = in_11; Enable_Inst = in_15;
  //   Enable_PC = in_13; Func_Code[5:0] = out_26; KDP_Avalible = in_17; KDP_Data[6:0] = in_16; NF = out_27;
  //   Op_Code_t[5:0] = out_22; pop = in_19; push = in_20; R_W = in_1; RAM_DATA[31:0] = in_14; Reset = in_18;
  //   RS_t[6:0] = out_28; TTY_DATA[6:0] = out_28; SE_Select = in_4; Value[31:0] = out_25; Value_Select = in_9;
  //   ZF = out_23

  // Notes on the sheet:
  //   Entradas
  //   DATA PATH
  //   COMPONENTES
  //   COMPLEMENTOS
  //   Salidas
endmodule

module ALU (
  input  [31:0] in_1,
  input  [31:0] in_2,
  input  [3:0] in_3,
  output [31:0] out_4,
  output [31:0] out_5,
  output [31:0] out_6,
  output out_7,
  output out_8
);

  wire comparator_1_lt, comparator_2_lt;
  wire [31:0] add, \and , Div, Divr, Divu, Divur, Mult, Multr, Mulu, Mulur, \nor , \or , slt, sltu, sub,
       \xor ;

  Multiplier #(.width(32)) multiplier_1 (.a(in_1), .b(in_2), .out(Mult), .cout(Multr));  // open: cin
  Mult_Signed mult_signed_1 (.in_1(in_1), .in_2(in_2), .out_3(Mulu), .out_4(Mulur));
  Div_Signed div_signed_1 (.in_1(in_1), .out_3(Divu), .in_2(in_2), .out_4(Divur));
  Divider #(.width(32)) divider_1 (.a(in_1), .b(in_2), .out(Div), .rem(Divr));  // open: upper
  Adder #(.width(32)) adder_1 (.a(in_1), .b(in_2), .out(add));  // open: cin, cout
  Subtractor #(.width(32)) subtractor_1 (.a(in_1), .b(in_2), .out(sub));  // open: bin, bout
  assign \and  = in_1 & in_2;  // AND_Gate and_1, 32 bits wide
  assign \or  = in_1 | in_2;  // OR_Gate or_1, 32 bits wide
  assign \nor  = ~(in_1 | in_2);  // NOR_Gate nor_1, 32 bits wide
  assign \xor  = in_1 ^ in_2;  // XOR_Gate xor_1, 32 bits wide
  Comparator #(.width(32)) comparator_1 (.a(in_1), .b(in_2), .lt(comparator_1_lt));  // open: gt, eq
  Comparator #(.width(32), .mode("unsigned")) comparator_2 (.a(in_1), .b(in_2), .lt(comparator_2_lt));  // open: gt, eq
  assign slt = {{31{1'b0}}, comparator_1_lt};  // Bit_Extender bit_extender_1
  assign sltu = {{31{1'b0}}, comparator_2_lt};  // Bit_Extender bit_extender_2
  Multiplexer #(.select(2), .width(32)) multiplexer_1 (
    .in0(Multr), .in1(Divr), .in2(Mulur), .in3(Divur), .out(out_5), .sel(in_3[1:0]));  // open: en
  Multiplexer #(.select(2), .width(32)) multiplexer_2 (
    .in0(Mult), .in1(Div), .in2(Mulu), .in3(Divu), .out(out_6), .sel(in_3[1:0]));  // open: en
  Comparator #(.width(32)) comparator_3 (.a({32{1'b0}}), .b(out_4), .eq(out_7));  // open: gt, lt
  Multiplexer #(.select(3), .width(32)) multiplexer_3 (
    .in0(add), .in1(sub), .in2(\and ), .in3(\or ), .in4(\nor ), .in5(\xor ), .in6(slt), .in7(sltu),
    .out(out_4), .sel(in_3[2:0]));  // open: en

  assign out_8 = out_4[0];

  // Other names for the same wires on the sheet: Hi[31:0] = out_5; Lo[31:0] = out_6; NF = out_4[0]; Rd[31:0] = out_4;
  //   Rs[31:0] = in_1; Rt[31:0] = in_2; Selector[2:0] = in_3[2:0]; Selector_ALU[3:0] = in_3;
  //   Selector_Hi_Lo[1:0] = in_3[1:0]; ZF = out_7

  // Notes on the sheet:
  //   Entradas
  //   ALU
  //   Salidas
endmodule

module Mult_Signed (
  input  [31:0] in_1,
  input  [31:0] in_2,
  output [31:0] out_3,
  output [31:0] out_4
);

  wire S_Sign;
  wire [31:0] adder_1_out, adder_2_out, Crry, Mult, multiplexer_1_out, multiplexer_2_out, not_1_out,
       not_2_out, nRs, nRt;

  Negator #(.width(32)) negator_1 (.in(in_1), .out(nRs));
  Negator #(.width(32)) negator_2 (.in(in_2), .out(nRt));
  Multiplexer #(.width(32)) multiplexer_1 (.in0(in_1), .in1(nRs), .out(multiplexer_1_out), .sel(in_1[31]));  // open: en
  Multiplexer #(.width(32)) multiplexer_2 (.in0(in_2), .in1(nRt), .out(multiplexer_2_out), .sel(in_2[31]));  // open: en
  xor xor_1 (S_Sign, in_1[31], in_2[31]);
  Multiplier #(.width(32)) multiplier_1 (
    .a(multiplexer_1_out), .b(multiplexer_2_out), .out(Mult), .cout(Crry));  // open: cin
  assign not_1_out = ~Mult;  // NOT_Gate not_1, 32 bits wide
  Adder #(.width(32)) adder_1 (.a(not_1_out), .b(32'h1), .out(adder_1_out));  // open: cin, cout
  assign not_2_out = ~Crry;  // NOT_Gate not_2, 32 bits wide
  Adder #(.width(32)) adder_2 (.a(not_2_out), .b(32'h1), .out(adder_2_out));  // open: cin, cout
  Multiplexer #(.width(32)) multiplexer_3 (.in0(Mult), .in1(adder_1_out), .out(out_3), .sel(S_Sign));  // open: en
  Multiplexer #(.width(32)) multiplexer_4 (.in0(Crry), .in1(adder_2_out), .out(out_4), .sel(S_Sign));  // open: en

  // Other names for the same wires on the sheet: Carry[31:0] = out_4; Rd[31:0] = out_3; Rs[31:0] = in_1;
  //   RsN = in_1[31]; Rt[31:0] = in_2; RtN = in_2[31]

  // Notes on the sheet:
  //   Entradas
  //   Multiplicador Signo
  //   Salidas
endmodule

module Div_Signed (
  input  [31:0] in_1,
  input  [31:0] in_2,
  output [31:0] out_3,
  output [31:0] out_4
);

  wire S_Sign;
  wire [31:0] Crry, Div, multiplexer_1_out, multiplexer_2_out, negator_3_out, negator_4_out, nRs, nRt;

  Negator #(.width(32)) negator_1 (.in(in_1), .out(nRs));
  Negator #(.width(32)) negator_2 (.in(in_2), .out(nRt));
  Multiplexer #(.width(32)) multiplexer_1 (.in0(in_1), .in1(nRs), .out(multiplexer_1_out), .sel(in_1[31]));  // open: en
  Multiplexer #(.width(32)) multiplexer_2 (.in0(in_2), .in1(nRt), .out(multiplexer_2_out), .sel(in_2[31]));  // open: en
  xor xor_1 (S_Sign, in_1[31], in_2[31]);
  Divider #(.width(32)) divider_1 (.a(multiplexer_1_out), .b(multiplexer_2_out), .out(Div), .rem(Crry));  // open: upper
  Negator #(.width(32)) negator_3 (.in(Div), .out(negator_3_out));
  Negator #(.width(32)) negator_4 (.in(Crry), .out(negator_4_out));
  Multiplexer #(.width(32)) multiplexer_3 (.in0(Div), .in1(negator_3_out), .out(out_3), .sel(S_Sign));  // open: en
  Multiplexer #(.width(32)) multiplexer_4 (.in0(Crry), .in1(negator_4_out), .out(out_4), .sel(S_Sign));  // open: en

  // Other names for the same wires on the sheet: Carry[31:0] = out_4; Rd[31:0] = out_3; Rs[31:0] = in_1;
  //   RsN = in_1[31]; Rt[31:0] = in_2; RtN = in_2[31]

  // Notes on the sheet:
  //   Entradas
  //   Divisor Signo
  //   Salidas
endmodule

module Register_File (
  input  [31:0] in_1,
  input  [4:0] in_2,
  input  [4:0] in_3,
  input  [4:0] in_4,
  input  in_5,
  input  in_6,
  input  in_7,
  input  in_8,
  input  in_9,
  output [31:0] out_10,
  output [31:0] out_11,
  output [31:0] out_12
);

  wire adder_1_cout, demultiplexer_1_out0, Enable_1, Enable_2, Enable_3, Enable_4, Enable_5, Enable_6,
       Enable_7, Enable_8, Enable_9, Enable_10, Enable_11, Enable_12, Enable_13, Enable_14, Enable_15,
       Enable_16, Enable_17, Enable_18, Enable_19, Enable_20, Enable_21, Enable_22, Enable_23, Enable_24,
       Enable_25, Enable_26, Enable_27, Enable_28, Enable_29, Enable_30, Enable_31, or_1_out;
  wire [1:0] priority_encoder_1_out;
  wire [31:0] adder_1_out, multiplexer_3_out, R0, R1, R2, R3, R4, R5, R6, R7, R8, R9, R10, R11, R12, R13,
       R14, R15, R16, R17, R18, R19, R20, R21, R22, R23, R24, R25, R26, R27, R28, R29, R30, R31,
       subtractor_1_out;

  Multiplexer #(.select(5), .width(32)) multiplexer_1 (
    .in0(R0), .in1(R1), .in2(R2), .in3(R3), .in4(R4), .in5(R5), .in6(R6), .in7(R7), .in8(R8), .in9(R9),
    .in10(R10), .in11(R11), .in12(R12), .in13(R13), .in14(R14), .in15(R15), .in16(R16), .in18(R18),
    .in19(R19), .in20(R20), .in21(R21), .in22(R22), .in23(R23), .in24(R24), .in25(R25), .in26(R26),
    .in27(R27), .in28(R28), .in29(R29), .in30(R30), .in31(R31), .out(out_10), .sel(in_2));  // open: in17, en
  Demultiplexer #(.select(5)) demultiplexer_1 (
    .out0(demultiplexer_1_out0), .out1(Enable_1), .out2(Enable_2), .out3(Enable_3), .out4(Enable_4),
    .out5(Enable_5), .out6(Enable_6), .out7(Enable_7), .out8(Enable_8), .out9(Enable_9), .out10(Enable_10),
    .out11(Enable_11), .out12(Enable_12), .out13(Enable_13), .out14(Enable_14), .out15(Enable_15),
    .out16(Enable_16), .out17(Enable_17), .out18(Enable_18), .out19(Enable_19), .out20(Enable_20),
    .out21(Enable_21), .out22(Enable_22), .out23(Enable_23), .out24(Enable_24), .out25(Enable_25),
    .out26(Enable_26), .out27(Enable_27), .out28(Enable_28), .out29(Enable_29), .out30(Enable_30),
    .out31(Enable_31), .in(in_7), .sel(in_4));  // open: en
  Multiplexer #(.select(5), .width(32)) multiplexer_2 (
    .in0(R0), .in1(R1), .in2(R2), .in3(R3), .in4(R4), .in5(R5), .in6(R6), .in7(R7), .in8(R8), .in9(R9),
    .in10(R10), .in11(R11), .in12(R12), .in13(R13), .in14(R14), .in15(R15), .in16(R16), .in18(R18),
    .in19(R19), .in20(R20), .in21(R21), .in22(R22), .in23(R23), .in24(R24), .in25(R25), .in26(R26),
    .in27(R27), .in28(R28), .in29(R29), .in30(R30), .in31(R31), .out(out_11), .sel(in_3));  // open: in17, en
  Register #(.width(32)) register_1 (.D({32{1'b0}}), .Q(R0), .clk(in_5), .clr(in_9));  // open: en
  Register #(.width(32)) register_2 (.D(in_1), .en(Enable_1), .Q(R1), .clk(in_5), .clr(in_9));
  Register #(.width(32)) register_3 (.D(in_1), .en(Enable_2), .Q(R2), .clk(in_5), .clr(in_9));
  Register #(.width(32)) register_4 (.D(in_1), .en(Enable_3), .Q(R3), .clk(in_5), .clr(in_9));
  Register #(.width(32)) register_5 (.D(in_1), .en(Enable_4), .Q(R4), .clk(in_5), .clr(in_9));
  Register #(.width(32)) register_6 (.D(in_1), .en(Enable_5), .Q(R5), .clk(in_5), .clr(in_9));
  Register #(.width(32)) register_7 (.D(in_1), .en(Enable_6), .Q(R6), .clk(in_5), .clr(in_9));
  Register #(.width(32)) register_8 (.D(in_1), .en(Enable_7), .Q(R7), .clk(in_5), .clr(in_9));
  Register #(.width(32)) register_9 (.D(in_1), .en(Enable_8), .Q(R8), .clk(in_5), .clr(in_9));
  Register #(.width(32)) register_10 (.D(in_1), .en(Enable_9), .Q(R9), .clk(in_5), .clr(in_9));
  Register #(.width(32)) register_11 (.D(in_1), .en(Enable_10), .Q(R10), .clk(in_5), .clr(in_9));
  Register #(.width(32)) register_12 (.D(in_1), .en(Enable_11), .Q(R11), .clk(in_5), .clr(in_9));
  Register #(.width(32)) register_13 (.D(in_1), .en(Enable_12), .Q(R12), .clk(in_5), .clr(in_9));
  Register #(.width(32)) register_14 (.D(in_1), .en(Enable_13), .Q(R13), .clk(in_5), .clr(in_9));
  Register #(.width(32)) register_15 (.D(in_1), .en(Enable_14), .Q(R14), .clk(in_5), .clr(in_9));
  Register #(.width(32)) register_16 (.D(in_1), .en(Enable_15), .Q(R15), .clk(in_5), .clr(in_9));
  Register #(.width(32)) register_17 (.D(in_1), .en(Enable_16), .Q(R16), .clk(in_5), .clr(in_9));
  Register #(.width(32)) register_18 (.D(in_1), .en(Enable_17), .Q(R17), .clk(in_5), .clr(in_9));
  Register #(.width(32)) register_19 (.D(in_1), .en(Enable_18), .Q(R18), .clk(in_5), .clr(in_9));
  Register #(.width(32)) register_20 (.D(in_1), .en(Enable_19), .Q(R19), .clk(in_5), .clr(in_9));
  Register #(.width(32)) register_21 (.D(in_1), .en(Enable_20), .Q(R20), .clk(in_5), .clr(in_9));
  Register #(.width(32)) register_22 (.D(in_1), .en(Enable_21), .Q(R21), .clk(in_5), .clr(in_9));
  Register #(.width(32)) register_23 (.D(in_1), .en(Enable_22), .Q(R22), .clk(in_5), .clr(in_9));
  Register #(.width(32)) register_24 (.D(in_1), .en(Enable_23), .Q(R23), .clk(in_5), .clr(in_9));
  Register #(.width(32)) register_25 (.D(in_1), .en(Enable_24), .Q(R24), .clk(in_5), .clr(in_9));
  Register #(.width(32)) register_26 (.D(in_1), .en(Enable_25), .Q(R25), .clk(in_5), .clr(in_9));
  Register #(.width(32)) register_27 (.D(in_1), .en(Enable_26), .Q(R26), .clk(in_5), .clr(in_9));
  Register #(.width(32)) register_28 (.D(in_1), .en(Enable_27), .Q(R27), .clk(in_5), .clr(in_9));
  Register #(.width(32)) register_29 (.D(in_1), .en(Enable_28), .Q(R28), .clk(in_5), .clr(in_9));
  Register #(.width(32)) register_30 (.D(in_1), .en(Enable_29), .Q(R29), .clk(in_5), .clr(in_9));
  Register #(.width(32)) register_31 (.D(in_1), .en(Enable_30), .Q(R30), .clk(in_5), .clr(in_9));
  Adder #(.width(32)) adder_1 (.a(R31), .b(32'h4), .out(adder_1_out), .cout(adder_1_cout));  // open: cin
  Subtractor #(.width(32)) subtractor_1 (.a(R31), .b(32'h4), .out(subtractor_1_out), .bin(adder_1_cout));  // open: bout
  Priority_Encoder #(.select(2)) priority_encoder_1 (
    .in0(1'b1), .in1(in_6), .in2(in_8), .in3(in_9), .out(priority_encoder_1_out));
  Multiplexer #(.select(2), .width(32)) multiplexer_3 (
    .in0(in_1), .in1(adder_1_out), .in2(subtractor_1_out), .in3(32'h3ffff), .out(multiplexer_3_out),
    .sel(priority_encoder_1_out));  // open: en
  or or_1 (or_1_out, in_6, in_8, Enable_31, in_9);
  Register #(.width(32)) register_32 (.D(multiplexer_3_out), .en(or_1_out), .Q(R31), .clk(in_5));  // open: clr

  // Other names for the same wires on the sheet: A[31:0] = out_10; B[31:0] = out_11; clk = in_5; Data[31:0] = in_1;
  //   pop = in_6; push = in_8; R_W = in_7; Reset = in_9; Selector_A[4:0] = in_2; Selector_B[4:0] = in_3;
  //   Selector_Data[4:0] = in_4; SP[31:0] = out_12

  // Notes on the sheet:
  //   Entradas
  //   A Selector
  //   B Selector
  //   Data Selector
  //   Registros
  //   Salidas
endmodule

module Program_Counter (
  input  [31:0] in_1,
  input  in_2,
  input  in_3,
  input  in_4,
  output [31:0] out_5
);

  Register #(.width(32)) register_1 (.D(in_1), .en(in_4), .Q(out_5), .clk(in_2), .clr(in_3));

  // Other names for the same wires on the sheet: clk = in_2; Data[31:0] = in_1; Enable = in_4; Reset = in_3

  // Notes on the sheet:
  //   PC
endmodule

module Intruction_Decoder (
  input  [31:0] in_1,
  output [5:0] out_2,
  output [4:0] out_3,
  output [4:0] out_4,
  output [25:0] out_5,
  output [4:0] out_6,
  output [15:0] out_7,
  output [5:0] out_8
);


  assign out_2 = in_1[31:26];
  assign out_3 = in_1[25:21];
  assign out_4 = in_1[20:16];
  assign out_5 = in_1[25:0];
  assign out_6 = in_1[15:11];
  assign out_7 = in_1[15:0];
  assign out_8 = in_1[5:0];

  // Other names for the same wires on the sheet: Constant[15:0] = in_1[15:0]; Func_Code[5:0] = in_1[5:0];
  //   Intruction[31:0] = in_1; Jump_Rute[25:0] = in_1[25:0]; Rd[4:0] = in_1[15:11]; Rt[4:0] = in_1[20:16];
  //   Rs[4:0] = in_1[25:21]; Op_Code[5:0] = in_1[31:26]

  // Notes on the sheet:
  //   Intruction Decoder
endmodule

module Branch_Control (
  input  [31:0] in_1,
  input  [25:0] in_2,
  input  [31:0] in_3,
  input  [2:0] in_4,
  input  [31:0] in_5,
  input  in_6,
  input  in_7,
  output [31:0] out_8
);

  wire and_1_out, and_2_out, and_3_out, and_4_out, and_5_out, beq, bgtz, blez, bltz, bne, brach_Jump, j, jr,
       nop, Rs____0;
  wire [1:0] S_Jump;
  wire [31:0] multiplier_1_out, PC___4, PC___4___4___Offset;

  Decoder #(.select(3)) decoder_1 (
    .out0(nop), .out1(beq), .out2(bne), .out3(blez), .out4(bgtz), .out5(bltz), .out6(j), .out7(jr), .sel(in_4));  // open: en
  and and_1 (and_1_out, beq, in_6);
  and and_2 (and_2_out, bne, ~in_6);  // AND_Gate
  and and_3 (and_3_out, blez, Rs____0);
  and and_4 (and_4_out, bgtz, ~Rs____0);  // AND_Gate
  and and_5 (and_5_out, bltz, in_7);
  Adder #(.width(32)) adder_1 (.a(in_1), .b(32'h4), .out(PC___4));  // open: cin, cout
  Multiplier #(.width(32)) multiplier_1 (.a(in_3), .b(32'h4), .out(multiplier_1_out));  // open: cin, cout
  Adder #(.width(32)) adder_2 (.a(PC___4), .b(multiplier_1_out), .out(PC___4___4___Offset));  // open: cin, cout
  or or_1 (Rs____0, in_6, in_7);
  or or_2 (brach_Jump, and_1_out, and_2_out, and_3_out, and_4_out, and_5_out);
  Priority_Encoder #(.select(2)) priority_encoder_1 (
    .in0(1'b1), .in1(brach_Jump), .in2(j), .in3(jr), .out(S_Jump), .en_in(1'b1));  // open: gs, en_out
  Multiplexer #(.select(2), .width(32)) multiplexer_1 (
    .in0(PC___4), .in1(PC___4___4___Offset), .in2({2'b00, in_2, in_1[3:0]}), .in3(in_5), .out(out_8),
    .sel(S_Jump));  // open: en

  // Other names for the same wires on the sheet: B_Selector[2:0] = in_4; Jump[29:0] = {in_2, in_1[3:0]};
  //   PC[31:0] = in_1; Rute[25:0] = in_2; NF = in_7; Offset[31:0] = in_3; PC_prime[31:0] = out_8; RS[31:0] = in_5;
  //   ZF = in_6

  // Notes on the sheet:
  //   Branch Control
endmodule

module Sign_Extender (
  input  [15:0] in_1,
  input  in_2,
  output [31:0] out_3
);

  wire [31:0] bit_extender_1_out, bit_extender_2_out;

  assign bit_extender_1_out = {{16{1'b0}}, in_1};  // Bit_Extender bit_extender_1
  assign bit_extender_2_out = {{16{in_1[15]}}, in_1};  // Bit_Extender bit_extender_2
  Multiplexer #(.width(32)) multiplexer_1 (
    .in0(bit_extender_1_out), .in1(bit_extender_2_out), .out(out_3), .sel(in_2));  // open: en

  // Other names for the same wires on the sheet: Input[15:0] = in_1; Output[31:0] = out_3; Sign = in_2

  // Notes on the sheet:
  //   Sign Extender
endmodule
